# Fritzing sketch MovementFritz (saved by Fritzing 0.9.4)
breadboards: 3

parts:
  Part1 = HC-SR501 Body Sensor Module
  Part2 = Arduino Uno (Rev3)
  J1 = Basic Servo
  Part3 = Breadboard Power Supply Board SMD  # not connected
  Part4 = Breadboard Power Supply Board SMD  # not connected
  VCC1 = Battery block 9V  # not connected
  VCC2 = Battery block 9V  # not connected
  U1 = ESP8266 WiFi Module [part_number=ESP8266]
  VCC3 = Battery block 9V  # not connected

nets:
  N1: Part1.OUT, Part2.D4
  N2: Part2.D3_PWM, J1.pulse
  N3: Part2.D6_PWM, U1.TXD
  N4: Part2.D7, U1.RXD
  3V3: Part2.3V3, U1.VCC
  GND: Part2.GND, U1.GND

custom parts:
  HC-SR501 Body Sensor Module: Pyroelectric Infrared PIR Motion Sensor Detector Module
